# Fritzing sketch LED_Button_Control_Schematic (saved by Fritzing 1.0.4)
breadboards: 1

parts:
  S2 = Pushbutton [package="[THT]"]
  Part1 = Arduino Uno (Rev3) - ICSP
  LED1 = smd LED [color="Green (565nm)" package="0805 [SMD]"]
  R1 = Resistor [tolerance=±5% resistance=220 package="2010 [SMD]"]

nets:
  N1: S2.Pin_1, S2.Pin_2, Part1.GND, R1.Pin_1
  N2: S2.Pin_3, S2.Pin_4, Part1.D8
  N3: Part1.D9_PWM, LED1.cathode
  N4: LED1.anode, R1.Pin_0
